// Logisim project main.circ as structural Verilog: 4 circuits, main circuit main
module main (
  input  Enable,
  input  Reset,
  output c0,
  output c1,
  output not_found,
  output found
);

  wire and_1_out, Clock_out, expected_output_1_out_5, or_1_out, success_1_found, validate_1_out_3;
  wire [1:0] Main_Counter_q;

  Clock Clock (.out(Clock_out));
  and and_1 (and_1_out, Clock_out, not_found, Enable);
  Counter #(.width(4), .max('hf), .ongoal("continue")) Main_Counter (
    .count(1'b1), .Q({c1, c0, Main_Counter_q}), .clk(and_1_out), .clr(Reset));  // open: load, D, carry
  expected_output expected_output_1 (
    .in_1(Main_Counter_q[0]), .in_2(Main_Counter_q[1]), .in_3(c0), .in_4(c1), .out_5(expected_output_1_out_5));
  not not_1 (not_found, found);
  or or_1 (or_1_out, Main_Counter_q[0], Main_Counter_q[1]);
  Validate validate_1 (.in_1(or_1_out), .in_2(expected_output_1_out_5), .out_3(validate_1_out_3));
  Success success_1 (.clk(and_1_out), .validate(validate_1_out_3), .found(success_1_found), .reset(Reset));
  and and_2 (found, Main_Counter_q[1], Main_Counter_q[0], success_1_found);
  // AND_Gate and_3 is placed but not wired
  // OR_Gate or_2 is placed but not wired
  // XOR_Gate xor_1 is placed but not wired
  // NAND_Gate nand_1 is placed but not wired

  // Notes on the sheet:
  //   Expected Output
  //   Test IC
  //   validate
  //   success
endmodule

module expected_output (
  input  in_1,
  input  in_2,
  input  in_3,
  input  in_4,
  output out_5
);


  assign out_5 = 1'b1;

  // Notes on the sheet:
  //   test case
  //   ic type
endmodule

module Validate (
  input  in_1,
  input  in_2,
  output out_3
);

  xnor xnor_1 (out_3, in_1, in_2);
endmodule

module Success (
  input  clk,
  input  validate,
  input  reset,
  output found
);

  wire and_1_out;

  and and_1 (and_1_out, validate, found);
  D_Flip_Flop d_ff_1 (.clk(clk), .D(and_1_out), .Q(found), .preset(reset));  // open: Qn, en, reset
endmodule
